// Logisim project FinalCircuit.circ as structural Verilog: 5 circuits, main circuit ALUForge
module ALUForge (
);

  ROM #(.dataWidth(16)) rom_1 ();  // open: addr, data
  registor PC ();  // open: CLOCK, WRITE, I0, I1, I2, I3, I4, I5, I6, I7, Sign, B0, B1, B2, B3, B4, B5, B6, B7, B8
  registor A ();  // open: CLOCK, WRITE, I0, I1, I2, I3, I4, I5, I6, I7, Sign, B0, B1, B2, B3, B4, B5, B6, B7, B8
  registor ACC ();  // open: CLOCK, WRITE, I0, I1, I2, I3, I4, I5, I6, I7, Sign, B0, B1, B2, B3, B4, B5, B6, B7, B8
  registor B ();  // open: CLOCK, WRITE, I0, I1, I2, I3, I4, I5, I6, I7, Sign, B0, B1, B2, B3, B4, B5, B6, B7, B8
endmodule

module registor (
  input  CLOCK,
  input  WRITE,
  input  I0,
  input  I1,
  input  I2,
  input  I3,
  input  I4,
  input  I5,
  input  I6,
  input  I7,
  input  Sign,
  output B0,
  output B1,
  output B2,
  output B3,
  output B4,
  output B5,
  output B6,
  output B7,
  output B8
);

  Dflipflop C1 (.CLOCK(CLOCK), .Write(WRITE), .D(I0), .val(B0));
  Dflipflop C2 (.CLOCK(CLOCK), .Write(WRITE), .D(I1), .val(B1));
  Dflipflop C3 (.CLOCK(CLOCK), .Write(WRITE), .D(I2), .val(B2));
  Dflipflop C4 (.CLOCK(CLOCK), .Write(WRITE), .D(I3), .val(B3));
  Dflipflop C5 (.CLOCK(CLOCK), .Write(WRITE), .D(I4), .val(B4));
  Dflipflop C6 (.CLOCK(CLOCK), .Write(WRITE), .D(I5), .val(B5));
  Dflipflop C7 (.CLOCK(CLOCK), .Write(WRITE), .D(I6), .val(B6));
  Dflipflop C8 (.CLOCK(CLOCK), .Write(WRITE), .D(I7), .val(B7));
  Dflipflop dflipflop_1 (.CLOCK(CLOCK), .Write(WRITE), .D(Sign), .val(B8));
endmodule

module Dflipflop (
  input  CLOCK,
  input  Write,
  input  D,
  output val
);

  wire and_1_out, nand_2_out, not_1_out, R_out, S_out;

  and and_1 (and_1_out, CLOCK, Write);
  not not_1 (not_1_out, D);
  nand S (S_out, D, and_1_out);
  nand R (R_out, and_1_out, not_1_out);
  nand nand_1 (val, S_out, nand_2_out);
  nand nand_2 (nand_2_out, val, R_out);
endmodule

module SUB_full (
  input  A,
  input  B,
  input  Bin,
  output D_out_aa112aa0,
  output Borrow
);

  Multiplexer #(.enable("true"), .select(3)) multiplexer_1 (
    .in0(1'b0), .in1(1'b1), .in2(1'b1), .in3(1'b0), .in4(1'b1), .in5(1'b0), .in6(1'b0), .in7(1'b1),
    .out(D_out_aa112aa0), .sel({A, B, Bin}));  // open: en
  Multiplexer #(.enable("true"), .select(3)) multiplexer_2 (
    .in0(1'b0), .in1(1'b1), .in2(1'b1), .in3(1'b1), .in4(1'b0), .in5(1'b0), .in6(1'b0), .in7(1'b1),
    .out(Borrow), .sel({A, B, Bin}));  // open: en
endmodule

module SUB (
  input  Borr_i,
  input  [7:0] A,
  input  [7:0] B,
  output [7:0] D,
  output Borrow
);

  wire sub_full_1_borrow, sub_full_2_borrow, sub_full_3_borrow, sub_full_4_borrow, sub_full_5_borrow,
       sub_full_6_borrow, sub_full_7_borrow;

  SUB_full sub_full_1 (.A(A[0]), .B(B[0]), .Bin(Borr_i), .D_out_aa112aa0(D[0]), .Borrow(sub_full_1_borrow));
  SUB_full sub_full_2 (.A(A[1]), .B(B[1]), .Bin(sub_full_1_borrow), .D_out_aa112aa0(D[1]), .Borrow(sub_full_2_borrow));
  SUB_full sub_full_3 (.A(A[2]), .B(B[2]), .Bin(sub_full_2_borrow), .D_out_aa112aa0(D[2]), .Borrow(sub_full_3_borrow));
  SUB_full sub_full_4 (.A(A[3]), .B(B[3]), .Bin(sub_full_3_borrow), .D_out_aa112aa0(D[3]), .Borrow(sub_full_4_borrow));
  SUB_full sub_full_5 (.A(A[4]), .B(B[4]), .Bin(sub_full_4_borrow), .D_out_aa112aa0(D[4]), .Borrow(sub_full_5_borrow));
  SUB_full sub_full_6 (.A(A[5]), .B(B[5]), .Bin(sub_full_5_borrow), .D_out_aa112aa0(D[5]), .Borrow(sub_full_6_borrow));
  SUB_full sub_full_7 (.A(A[6]), .B(B[6]), .Bin(sub_full_6_borrow), .D_out_aa112aa0(D[6]), .Borrow(sub_full_7_borrow));
  SUB_full sub_full_8 (.A(A[7]), .B(B[7]), .Bin(sub_full_7_borrow), .D_out_aa112aa0(D[7]), .Borrow(Borrow));
endmodule
